# Fritzing sketch solarHeaterController (saved by Fritzing 0.9.3b)
breadboards: 1

parts:
  Part1 = Arduino Uno (Rev3)
  Part2 = Adafruit MAX31865 RTD Sensor Breakout [part_number="Adafruit #3328"]
  Part3 = Adafruit MAX31865 RTD Sensor Breakout [part_number="Adafruit #3328"]
  Raspberry_Pi1 = Raspberry Pi 2
  U1 = RELAY-SOLIDSTATE [package=relay-s108t02]
  R1 = Temperature Sensor (Thermistor) [thermistor_type=NTC package=THT]
  R2 = Temperature Sensor (Thermistor) [thermistor_type=NTC package=THT]
  M1 = DC Motor

nets:
  N1: Part1.A4/SDA, Raspberry_Pi1.GPIO2
  N2: Part1.A5/SCL, Raspberry_Pi1.GPIO3
  N3: Part1.D9_PWM, Part3.CS
  N4: Part1.D10_PWM/SS, Part2.CS
  N5: Part1.D11_PWM/MOSI, Part2.SDI, Part3.SDI
  N6: Part1.D12/MISO, Part2.SDO, Part3.SDO
  N7: Part1.D13/SCK, Part2.SCLK, Part3.SCLK
  N8: Part1.D2, U1.+
  N9: Part1.D3_PWM, M1.pin_1
  5V: Part1.5V, Part2.VIN, Part3.VIN, Raspberry_Pi1.5V
  GND: Part1.GND, Part2.GND, Part3.GND, Raspberry_Pi1.GND, U1.-, M1.pin_2
  N10: Part2.RTDIN+, R2.pin_1
  N11: Part2.RTDIN-, R2.pin_0
  N12: Part3.RTDIN+, R1.pin_1
  N13: Part3.RTDIN-, R1.pin_0

custom parts:
  Adafruit MAX31865 RTD Sensor Breakout: For precision temperature sensing, nothing beats a Platinum RTD. Resistance temperature detectors (RTDs) are temperature sensors that contain a resistor that changes resistance value as its temperature changes, basically a kind of thermistor. In this sensor, the resistor is actually a small strip of Platinum with a resistance of 100 ohms at 0°C, thus the name PT100. Compared to most NTC/PTC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
